# Fritzing sketch Arduino_Uno_i2C_LCD (saved by Fritzing 0.9.3b)
circuit board: 8.46667cm x 5.64444cm
breadboards: 1

parts:
  Onderdeel1 = Arduino Uno (Rev3)
  LCM1602_IIC1 = LCM1602 IIC [part_number="LCM1602 IIC" chip_label="LCM1602 IIC" package="DIP (Dual Inline) [THT]"]
  LCD1 = LCD screen
  M1 = pcf8574 io expansion board [package=THT]
  Pololu_A1 = Pololu A4988 [package=SO16]
  M2 = Stepper Motor - Bipolar
  12_V_for_Strepper_Motor = Power Jack [package=power_jack_combo]

nets (from the breadboard view):
  N1: Onderdeel1.D4, LCM1602_IIC1.SDA
  N2: Onderdeel1.D5_PWM, LCM1602_IIC1.SCL
  VCC: Onderdeel1.5V, LCM1602_IIC1.VCC, M1.VCC, Pololu_A1.VDD
  GND: Onderdeel1.GND, LCM1602_IIC1.GND, M1.GND, Pololu_A1.GND#8
  VSS: LCM1602_IIC1.VSS, LCD1.VSS
  VDD: LCM1602_IIC1.VDD, LCD1.VDD
  N3: LCM1602_IIC1.V0, LCD1.V0
  N4: LCM1602_IIC1.RS, LCD1.RS
  N5: LCM1602_IIC1.RW, LCD1.R/W
  N6: LCM1602_IIC1.E, LCD1.E
  N7: LCM1602_IIC1.D0, LCD1.DB0
  N8: LCM1602_IIC1.D1, LCD1.DB1
  N9: LCM1602_IIC1.D2, LCD1.DB2
  N10: LCM1602_IIC1.D3, LCD1.DB3
  N11: LCM1602_IIC1.D4, LCD1.DB4
  N12: LCM1602_IIC1.D5, LCD1.DB5
  N13: LCM1602_IIC1.D6, LCD1.DB6
  N14: LCM1602_IIC1.D7, LCD1.DB7
  N15: LCM1602_IIC1.A, LCD1.LED+
  N16: LCM1602_IIC1.K, LCD1.LED-
  N17: LCM1602_IIC1.LED_A, LCM1602_IIC1.LED_B
  N18: M1.O0, Pololu_A1.STEP
  N19: M1.O1, Pololu_A1.DIR
  N20: Pololu_A1.1B, M2.A
  N21: Pololu_A1.1A, M2.C
  N22: Pololu_A1.2A, M2.B
  N23: Pololu_A1.2B, M2.D
  N24: Pololu_A1.GND#14, 12_V_for_Strepper_Motor.GND
  N25: Pololu_A1.VMOT, 12_V_for_Strepper_Motor.PWR

custom parts:
  LCM1602 IIC: I2C-Module to use a 1602 or 2004 LCD on with the wire.h libory Serial LCD Modul
  pcf8574 io expansion board: pcf8574 io expansion board.

// code stored in the sketch: AnalogReadSerial2LCD_LED.ino
#define SDA_PIN 4  // Define the SDA pin
#define SCL_PIN 5  // Define the SCL pin


#define LCD_ADDR 0x3F
#define BACKLIGHT 0x08
#define EN 0x04
#define STEPPER_ADDR 0x20
String inputString = "";         // a String to hold incoming data
bool stringComplete = false;     // whether the string is complete


void moveStepper(int steps) {
  int direction = steps > 0 ? 1 : 0; // Set direction


  for (int i = 0; i < abs(steps); i++) {
    // Set direction and make a step
    uint8_t command = (direction << 0) | (1 << 1); // P0 controls DIR, P1 controls STEP
    i2cStart();
    i2cSendByte((STEPPER_ADDR << 1) | 0); // Send the address for write
    i2cSendByte(command);
    i2cStop();
    delay(2); // Add a delay to control the speed of the steps


    // Reset STEP pin
    command = (direction << 0); 
    i2cStart();
    i2cSendByte((STEPPER_ADDR << 1) | 0); // Send the address for write
    i2cSendByte(command);
    i2cStop();
    delay(2);
  }
}
void controlA4988(bool enable, bool direction) {
  uint8_t controlPins = 0x00;
  if (enable) {
    controlPins |= 0b00000010; // Set the Enable pin (p1) to enable the driver
  }
  if (direction) {
    controlPins |= 0b00000001; // Set the Direction pin (p0) for desired direction
  }
  
  // Send the control pins to PCF8574
  i2cStart();
  i2cSendByte((STEPPER_ADDR << 1) | 0); // Send the address for write
  i2cSendByte(controlPins);
  i2cStop();
}



void setup() {
  pinMode(SDA_PIN, OUTPUT);
  pinMode(SCL_PIN, OUTPUT);
delay(1000); 
  Serial.begin(9600);  // Initialize serial communication


  // Initial message on Serial Monitor
  Serial.println("Send a string to display on the LCD:");


  i2cStart();
  i2cSendByte((LCD_ADDR << 1) | 0); 
  i2cStop();


  initLCD();
    moveStepper(1); // Move one step forward
  sendStringToLCD("Stepper Moved!");
  Serial.println("Stepper Moved");


}


void loop() {
  // Check if we received a full string from Serial Monitor
  if (stringComplete) {
    sendStringToLCD(0x01);  // Clear the display
    sendStringToLCD(inputString.c_str());  // Display string on LCD
    inputString = "";  // Clear the string
    stringComplete = false;  // Reset the flag
  }
}
void serialEvent() {
  while (Serial.available()) {
    char inChar = (char)Serial.read();
    inputString += inChar;


    if (inChar == '\n') {
      stringComplete = true;
    }
  }
}


void i2cStart() {
  digitalWrite(SDA_PIN, HIGH);
  digitalWrite(SCL_PIN, HIGH);
  digitalWrite(SDA_PIN, LOW);
  digitalWrite(SCL_PIN, LOW);
}


void i2cStop() {
  digitalWrite(SDA_PIN, LOW);
  digitalWrite(SCL_PIN, HIGH);
  digitalWrite(SDA_PIN, HIGH);
}


void i2cSendByte(uint8_t data) {
  for (int i = 0; i < 8; i++) {
    if (data & 0x80)
      digitalWrite(SDA_PIN, HIGH);
    else
      digitalWrite(SDA_PIN, LOW);
    data <<= 1;
    digitalWrite(SCL_PIN, HIGH);
    digitalWrite(SCL_PIN, LOW);
  }


  // Acknowledgment
  pinMode(SDA_PIN, INPUT);
  digitalWrite(SCL_PIN, HIGH);
  while (digitalRead(SDA_PIN));
  digitalWrite(SCL_PIN, LOW);
  pinMode(SDA_PIN, OUTPUT);
}


void sendToLCD(uint8_t data, bool isChar = false) {
  uint8_t upperNibble = data & 0xF0;
  uint8_t lowerNibble = (data << 4) & 0xF0;


  i2cStart();
  i2cSendByte((LCD_ADDR << 1) | 0); 
  i2cSendByte(upperNibble | BACKLIGHT | (isChar ? 0x01 : 0x00));
  i2cSendByte(upperNibble | BACKLIGHT | EN | (isChar ? 0x01 : 0x00));
  i2cSendByte(upperNibble | BACKLIGHT | (isChar ? 0x01 : 0x00));
  
  i2cSendByte(lowerNibble | BACKLIGHT | (isChar ? 0x01 : 0x00));
  i2cSendByte(lowerNibble | BACKLIGHT | EN | (isChar ? 0x01 : 0x00));
  i2cSendByte(lowerNibble | BACKLIGHT | (isChar ? 0x01 : 0x00));
  i2cStop();
}


void initLCD() {
  sendToLCD(0x33); 
  sendToLCD(0x32);
  sendToLCD(0x28); 
  sendToLCD(0x0C); 
  sendToLCD(0x06); 
  sendToLCD(0x01); 
  delay(5);
}


void sendStringToLCD(const char *str) {
  while (*str) {
    sendToLCD(*str, true);
    str++;
  }
}
